// Logisim project control-logic.circ as structural Verilog: 1 circuit, main circuit control_logic
module control_logic (
  input  [31:0] Instruction,
  input  BrEq,
  input  BrLt,
  output PCSel,
  output RegWEn,
  output [2:0] ImmSel,
  output BrUn,
  output ASel,
  output BSel,
  output [3:0] ALUSel,
  output MemWEn,
  output [1:0] WBSel
);

  wire add, addi, and0, and_1_out, and_2_out, and_3_out, and_4_out, andi, auipc, beq, bge, bgeu, blt, bltu,
       bne, comparator_1_eq, comparator_2_eq, comparator_3_eq, comparator_4_eq, comparator_5_eq,
       demultiplexer_1_out5, demultiplexer_2_out0, demultiplexer_2_out1, demultiplexer_2_out5, jal, jalr, lb,
       lh, lui, lw, mul, mulh, mulhu, not_1_out, not_2_out, or0, or_1_out, or_2_out, or_3_out, or_4_out, ori,
       sb, sh, sll0, slli, slt, slti, sra0, srai, srl0, srli, sub, sw, xor0, xori;
  wire [5:0] ROMInput;
  wire [15:14] rom_1_data;

  Demultiplexer #(.select(3)) demultiplexer_1 (
    .out0(addi), .out1(slli), .out2(slti), .out4(xori), .out5(demultiplexer_1_out5), .out6(ori), .out7(andi),
    .in(comparator_1_eq), .sel(Instruction[14:12]));  // open: out3
  Comparator #(.width(7)) comparator_1 (.a(Instruction[6:0]), .b(7'b0010011), .eq(comparator_1_eq));  // open: gt, lt
  Demultiplexer #(.select(3)) demultiplexer_2 (
    .out0(demultiplexer_2_out0), .out1(demultiplexer_2_out1), .out2(slt), .out3(mulhu), .out4(xor0),
    .out5(demultiplexer_2_out5), .out6(or0), .out7(and0), .in(comparator_2_eq), .sel(Instruction[14:12]));
  Comparator #(.width(7)) comparator_2 (.a(Instruction[6:0]), .b(7'b0110011), .eq(comparator_2_eq));  // open: gt, lt
  Demultiplexer #(.select(3)) demultiplexer_3 (
    .out0(beq), .out1(bne), .out4(blt), .out5(bge), .out6(bltu), .out7(bgeu), .in(comparator_3_eq),
    .sel(Instruction[14:12]));  // open: out2, out3
  Comparator #(.width(7)) comparator_3 (.a(Instruction[6:0]), .b(7'b1100011), .eq(comparator_3_eq));  // open: gt, lt
  Demultiplexer #(.select(3)) demultiplexer_4 (
    .out0(lb), .out1(lh), .out2(lw), .in(comparator_4_eq), .sel(Instruction[14:12]));  // open: out3, out4, out5, out6, out7
  Comparator #(.width(7)) comparator_4 (.a(Instruction[6:0]), .b(7'b0000011), .eq(comparator_4_eq));  // open: gt, lt
  Demultiplexer #(.select(3)) demultiplexer_5 (
    .out0(sb), .out1(sh), .out2(sw), .in(comparator_5_eq), .sel(Instruction[14:12]));  // open: out3, out4, out5, out6, out7
  Comparator #(.width(7)) comparator_5 (.a(Instruction[6:0]), .b(7'b0100011), .eq(comparator_5_eq));  // open: gt, lt
  Comparator #(.width(7)) comparator_6 (.a(Instruction[6:0]), .b(7'b0010111), .eq(auipc));  // open: gt, lt
  Comparator #(.width(7)) comparator_7 (.a(Instruction[6:0]), .b(7'b0110111), .eq(lui));  // open: gt, lt
  Comparator #(.width(7)) comparator_8 (.a(Instruction[6:0]), .b(7'b1101111), .eq(jal));  // open: gt, lt
  Comparator #(.width(7)) comparator_9 (.a(Instruction[6:0]), .b(7'b1100111), .eq(jalr));  // open: gt, lt
  ROM #(.addrWidth(6), .dataWidth(16)) rom_1 (
    .addr(ROMInput), .data({rom_1_data, WBSel, MemWEn, ALUSel, BSel, ASel, BrUn, ImmSel, RegWEn}));
  Demultiplexer demultiplexer_6 (.out0(srli), .out1(srai), .in(demultiplexer_1_out5), .sel(Instruction[30]));
  Demultiplexer demultiplexer_7 (.out0(srl0), .out1(sra0), .in(demultiplexer_2_out5), .sel(Instruction[30]));
  Demultiplexer #(.select(2)) demultiplexer_8 (
    .out0(add), .out1(mul), .out2(sub), .in(demultiplexer_2_out0), .sel({Instruction[30], Instruction[25]}));  // open: out3
  Demultiplexer demultiplexer_9 (.out0(sll0), .out1(mulh), .in(demultiplexer_2_out1), .sel(Instruction[25]));
  not not_1 (not_1_out, BrEq);
  or or_1 (or_1_out, blt, bltu);
  or or_2 (or_2_out, bge, bgeu);
  not not_2 (not_2_out, BrLt);
  and and_1 (and_1_out, beq, BrEq);
  and and_2 (and_2_out, bne, not_1_out);
  and and_3 (and_3_out, or_1_out, BrLt);
  and and_4 (and_4_out, or_2_out, not_2_out);
  or or_3 (or_3_out, jal, jalr);
  or or_4 (or_4_out, and_1_out, and_2_out, and_3_out, and_4_out);
  or or_5 (PCSel, or_4_out, or_3_out);
  Priority_Encoder #(.select_enc(6)) priority_encoder_1 (
    .in0(add), .in1(mul), .in2(sub), .in3(sll0), .in4(mulh), .in5(mulhu), .in6(slt), .in7(xor0), .in8(srl0),
    .in9(sra0), .in10(or0), .in11(and0), .in12(lb), .in13(lh), .in14(lw), .in15(addi), .in16(slli),
    .in17(slti), .in18(xori), .in19(srli), .in20(srai), .in21(ori), .in22(andi), .in23(sb), .in24(sh),
    .in25(sw), .in26(beq), .in27(bne), .in28(blt), .in29(bge), .in30(bltu), .in31(bgeu), .in32(auipc),
    .in33(lui), .in34(jal), .in35(jalr), .out(ROMInput));  // open: in36, in37, in38, in39, in40, in41, in42, in43, in44, in45, in46, in47, in48, in49, in50, in51, in52, in53, in54, in55, in56, in57, in58, in59, in60, in61, in62, in63, gs, en_out, en_in

  // Other names for the same wires on the sheet: opcode[6:0] = Instruction[6:0]; funct3[2:0] = Instruction[14:12];
  //   funct7[6:0] = Instruction[31:25]

  // Notes on the sheet:
  //   INPUTS to your circuit
  //   contents of rom_1 (hex, n*v repeats v):
  //   1001 1401 1601 1081 1481 1581 1101 1201 1281 1681 1301 1381 841 841 841 1041 10c1 1141 1241 12c1
  //   16c1 1341 13c1 842 842 842 4*64 74 74 1067 17c7 2069 2041
  //   ROM FOR CONTROL LOGIC
  //   DON'T CHANGE THE LOCATIONS OF THE INPUTS AND OUTPUTS!
  //   This is only if you choose to do the ROM option
  //   OUTPUT from your circuit
  //   Reminder: If using ROM, use combinational logic for PCSel
endmodule
