// Logisim project cpu.circ as structural Verilog: 1 circuit, main circuit cpu
module cpu (
  input  clk,
  input  [31:0] Instruction,
  input  [31:0] MemReadData,
  output [31:0] MemAddress,
  output [31:0] ProgramCounter,
  output [31:0] ra,
  output [31:0] sp,
  output [31:0] t0,
  output [31:0] t1,
  output [31:0] t2,
  output [31:0] s0,
  output [31:0] s1,
  output [31:0] a0,
  output [3:0] MemWriteMask,
  output [31:0] MemWriteData
);

  wire ASel, BrEq, BrLt, BrUn, BSel, MemWEn, PCSel, RegWEn;
  wire [1:0] WBSel;
  wire [2:0] funct3, ImmSel;
  wire [3:0] ALUSel;
  wire [31:0] A, B, imm, InstructionStage2, Mem, multiplexer_2_out, NewPC, PCplus4, PCplus4Stage2,
       ProgramCounterStage2, ReadData1, ReadData2, WB;

  Adder #(.width(32)) adder_1 (.a(ProgramCounter), .b(32'h4), .out(PCplus4));  // open: cin, cout
  Register #(.width(32)) PC (.D(NewPC), .clk(clk), .Q(ProgramCounter));  // open: en, clr
  Multiplexer #(.width(32)) multiplexer_1 (.in0(PCplus4), .in1(MemAddress), .out(NewPC), .sel(PCSel));
  Register #(.width(32)) register_1 (.D(ProgramCounter), .clk(clk), .Q(ProgramCounterStage2));  // open: en, clr
  Adder #(.width(32)) adder_2 (.a(ProgramCounterStage2), .b(32'h4), .out(PCplus4Stage2));  // open: cin, cout
  control_logic control_logic_1 (
    .Instruction({InstructionStage2[31:15], funct3, InstructionStage2[11:0]}), .BrEq(BrEq), .BrLt(BrLt),
    .PCSel(PCSel), .RegWEn(RegWEn), .ImmSel(ImmSel), .BrUn(BrUn), .ASel(ASel), .BSel(BSel), .ALUSel(ALUSel),
    .MemWEn(MemWEn), .WBSel(WBSel));
  Multiplexer #(.width(32)) multiplexer_2 (.in0(Instruction), .in1(32'h13), .out(multiplexer_2_out), .sel(PCSel));
  regfile regfile_1 (
    .ReadIndex1(InstructionStage2[19:15]), .ReadIndex2(InstructionStage2[24:20]),
    .WriteIndex(InstructionStage2[11:7]), .WriteData(WB), .RegWEn(RegWEn), .clk(clk), .ra(ra), .sp(sp),
    .t0(t0), .t1(t1), .t2(t2), .s0(s0), .s1(s1), .a0(a0), .ReadData1(ReadData1), .ReadData2(ReadData2));
  imm_gen imm_gen_1 (
    .Instruction({InstructionStage2[31:15], funct3, InstructionStage2[11:0]}), .ImmSel(ImmSel),
    .Immediate(imm));
  Register #(.width(32)) register_2 (
    .D(multiplexer_2_out), .clk(clk), .Q({InstructionStage2[31:15], funct3, InstructionStage2[11:0]}));  // open: en, clr
  branch_comp branch_comp_1 (.BrData1(ReadData1), .BrData2(ReadData2), .BrUn(BrUn), .BrEq(BrEq), .BrLt(BrLt));
  alu alu_1 (.A(A), .B(B), .ALUSel(ALUSel), .ALUResult(MemAddress));
  Multiplexer #(.width(32)) multiplexer_3 (.in0(ReadData1), .in1(ProgramCounterStage2), .out(A), .sel(ASel));
  Multiplexer #(.width(32)) multiplexer_4 (.in0(ReadData2), .in1(imm), .out(B), .sel(BSel));
  Multiplexer #(.select(2), .width(32)) multiplexer_5 (
    .in0(Mem), .in1(MemAddress), .in2(PCplus4Stage2), .out(WB), .sel(WBSel));  // open: in3
  partial_store partial_store_1 (
    .Instruction({InstructionStage2[31:15], funct3, InstructionStage2[11:0]}), .MemAddress(MemAddress),
    .DataFromReg(ReadData2), .MemWEn(MemWEn), .MemWriteMask(MemWriteMask), .DataToMem(MemWriteData));
  partial_load partial_load_1 (
    .Instruction({InstructionStage2[31:15], funct3, InstructionStage2[11:0]}), .MemAddress(MemAddress),
    .DataFromMem(MemReadData), .DataToReg(Mem));

  // Other names for the same wires on the sheet: ALUResult[31:0] = MemAddress; opcode[6:0] = InstructionStage2[6:0];
  //   rd[4:0] = InstructionStage2[11:7]; InstructionStage2[14:12] = funct3; rs1[4:0] = InstructionStage2[19:15];
  //   rs2[4:0] = InstructionStage2[24:20]

  // Notes on the sheet:
  //   To IMEM
  //   IMEM (do **NOT** move this)
  //   From IMEM
  //   Inputs/Outputs for testing. Do **NOT** move these.
  //   It is OK to move the PC, RegFile, ALU, MEM, Branch Comp, Imm Gen, Partial Load, Partial Store and Control Logic to wherever is most convenient for you when constructing your CPU, and to delete this text
  //   To DMEM
  //   DMEM (do **NOT** move this)
  //   From DMEM
endmodule
