// Logisim project regfile.circ as structural Verilog: 1 circuit, main circuit regfile
module regfile (
  input  [4:0] ReadIndex1,
  input  [4:0] ReadIndex2,
  input  [4:0] WriteIndex,
  input  [31:0] WriteData,
  input  RegWEn,
  input  clk,
  output [31:0] ra,
  output [31:0] sp,
  output [31:0] t0,
  output [31:0] t1,
  output [31:0] t2,
  output [31:0] s0,
  output [31:0] s1,
  output [31:0] a0,
  output [31:0] ReadData1,
  output [31:0] ReadData2
);

  wire e0, e1, e2, e3, e4, e5, e6, e7, e8, e9, e10, e11, e12, e13, e14, e15, e16, e17, e18, e19, e20, e21,
       e22, e23, e24, e25, e26, e27, e28, e29, e30, e31;
  wire [31:0] r0, r3, r4, r11, r12, r13, r14, r15, r16, r17, r18, r19, r20, r21, r22, r23, r24, r25, r26,
       r27, r28, r29, r30, r31, w1, w2, w3, w4, w5, w6, w7, w8, w9, w10, w11, w12, w13, w14, w15, w16, w17,
       w18, w19, w20, w21, w22, w23, w24, w25, w26, w27, w28, w29, w30, w31;

  Multiplexer #(.select(5), .width(32)) multiplexer_1 (
    .in0(r0), .in1(ra), .in2(sp), .in3(r3), .in4(r4), .in5(t0), .in6(t1), .in7(t2), .in8(s0), .in9(s1),
    .in10(a0), .in11(r11), .in12(r12), .in13(r13), .in14(r14), .in15(r15), .in16(r16), .in17(r17),
    .in18(r18), .in19(r19), .in20(r20), .in21(r21), .in22(r22), .in23(r23), .in24(r24), .in25(r25),
    .in26(r26), .in27(r27), .in28(r28), .in29(r29), .in30(r30), .in31(r31), .out(ReadData1), .sel(ReadIndex1));
  Multiplexer #(.select(5), .width(32)) multiplexer_2 (
    .in0(r0), .in1(ra), .in2(sp), .in3(r3), .in4(r4), .in5(t0), .in6(t1), .in7(t2), .in8(s0), .in9(s1),
    .in10(a0), .in11(r11), .in12(r12), .in13(r13), .in14(r14), .in15(r15), .in16(r16), .in17(r17),
    .in18(r18), .in19(r19), .in20(r20), .in21(r21), .in22(r22), .in23(r23), .in24(r24), .in25(r25),
    .in26(r26), .in27(r27), .in28(r28), .in29(r29), .in30(r30), .in31(r31), .out(ReadData2), .sel(ReadIndex2));
  Register #(.width(32)) register_1 (.D({32{1'b0}}), .en(e0), .clk(clk), .Q(r0));  // open: clr
  Register #(.width(32)) register_2 (.D(w1), .en(e1), .clk(clk), .Q(ra));  // open: clr
  Register #(.width(32)) register_3 (.D(w2), .en(e2), .clk(clk), .Q(sp));  // open: clr
  Register #(.width(32)) register_4 (.D(w3), .en(e3), .clk(clk), .Q(r3));  // open: clr
  Register #(.width(32)) register_5 (.D(w4), .en(e4), .clk(clk), .Q(r4));  // open: clr
  Register #(.width(32)) register_6 (.D(w5), .en(e5), .clk(clk), .Q(t0));  // open: clr
  Register #(.width(32)) register_7 (.D(w6), .en(e6), .clk(clk), .Q(t1));  // open: clr
  Register #(.width(32)) register_8 (.D(w7), .en(e7), .clk(clk), .Q(t2));  // open: clr
  Register #(.width(32)) register_9 (.D(w8), .en(e8), .clk(clk), .Q(s0));  // open: clr
  Register #(.width(32)) register_10 (.D(w9), .en(e9), .clk(clk), .Q(s1));  // open: clr
  Register #(.width(32)) register_11 (.D(w10), .en(e10), .clk(clk), .Q(a0));  // open: clr
  Register #(.width(32)) register_12 (.D(w11), .en(e11), .clk(clk), .Q(r11));  // open: clr
  Register #(.width(32)) register_13 (.D(w12), .en(e12), .clk(clk), .Q(r12));  // open: clr
  Register #(.width(32)) register_14 (.D(w13), .en(e13), .clk(clk), .Q(r13));  // open: clr
  Register #(.width(32)) register_15 (.D(w14), .en(e14), .clk(clk), .Q(r14));  // open: clr
  Register #(.width(32)) register_16 (.D(w15), .en(e15), .clk(clk), .Q(r15));  // open: clr
  Register #(.width(32)) register_17 (.D(w16), .en(e16), .clk(clk), .Q(r16));  // open: clr
  Register #(.width(32)) register_18 (.D(w17), .en(e17), .clk(clk), .Q(r17));  // open: clr
  Register #(.width(32)) register_19 (.D(w18), .en(e18), .clk(clk), .Q(r18));  // open: clr
  Register #(.width(32)) register_20 (.D(w19), .en(e19), .clk(clk), .Q(r19));  // open: clr
  Register #(.width(32)) register_21 (.D(w20), .en(e20), .clk(clk), .Q(r20));  // open: clr
  Register #(.width(32)) register_22 (.D(w21), .en(e21), .clk(clk), .Q(r21));  // open: clr
  Register #(.width(32)) register_23 (.D(w22), .en(e22), .clk(clk), .Q(r22));  // open: clr
  Register #(.width(32)) register_24 (.D(w23), .en(e23), .clk(clk), .Q(r23));  // open: clr
  Register #(.width(32)) register_25 (.D(w24), .en(e24), .clk(clk), .Q(r24));  // open: clr
  Register #(.width(32)) register_26 (.D(w25), .en(e25), .clk(clk), .Q(r25));  // open: clr
  Register #(.width(32)) register_27 (.D(w26), .en(e26), .clk(clk), .Q(r26));  // open: clr
  Register #(.width(32)) register_28 (.D(w27), .en(e27), .clk(clk), .Q(r27));  // open: clr
  Register #(.width(32)) register_29 (.D(w28), .en(e28), .clk(clk), .Q(r28));  // open: clr
  Register #(.width(32)) register_30 (.D(w29), .en(e29), .clk(clk), .Q(r29));  // open: clr
  Register #(.width(32)) register_31 (.D(w30), .en(e30), .clk(clk), .Q(r30));  // open: clr
  Register #(.width(32)) register_32 (.D(w31), .en(e31), .clk(clk), .Q(r31));  // open: clr
  Demultiplexer #(.select(5), .width(32)) demultiplexer_1 (
    .out1(w1), .out2(w2), .out3(w3), .out4(w4), .out5(w5), .out6(w6), .out7(w7), .out8(w8), .out9(w9),
    .out10(w10), .out11(w11), .out12(w12), .out13(w13), .out14(w14), .out15(w15), .out16(w16), .out17(w17),
    .out18(w18), .out19(w19), .out20(w20), .out21(w21), .out22(w22), .out23(w23), .out24(w24), .out25(w25),
    .out26(w26), .out27(w27), .out28(w28), .out29(w29), .out30(w30), .out31(w31), .in(WriteData),
    .sel(WriteIndex));  // open: out0
  Demultiplexer #(.select(5)) demultiplexer_2 (
    .out0(e0), .out1(e1), .out2(e2), .out3(e3), .out4(e4), .out5(e5), .out6(e6), .out7(e7), .out8(e8),
    .out9(e9), .out10(e10), .out11(e11), .out12(e12), .out13(e13), .out14(e14), .out15(e15), .out16(e16),
    .out17(e17), .out18(e18), .out19(e19), .out20(e20), .out21(e21), .out22(e22), .out23(e23), .out24(e24),
    .out25(e25), .out26(e26), .out27(e27), .out28(e28), .out29(e29), .out30(e30), .out31(e31), .in(RegWEn),
    .sel(WriteIndex));

  // Other names for the same wires on the sheet: r1[31:0] = ra; r2[31:0] = sp; r5[31:0] = t0; r6[31:0] = t1;
  //   r7[31:0] = t2; r8[31:0] = s0; r9[31:0] = s1; r10[31:0] = a0

  // Notes on the sheet:
  //   INPUTS to your circuit
  //   DON'T CHANGE THE LOCATIONS OF THE INPUTS AND OUTPUTS!
  //   These are DEBUG/TEST outputs from your circuit.
  //   OUTPUTS from your circuit
endmodule
